// Logisim project e2448397.circ as structural Verilog: 1 circuit, main circuit main
module main (
  input  O2,
  input  O1,
  input  O0,
  input  A1,
  input  A0,
  input  B1,
  input  B0,
  output S,
  output L6,
  output L5,
  output L4,
  output L3,
  output L2,
  output L1,
  output L0
);

  wire n3_to_8_decoder_74138_1_p4, n3_to_8_decoder_74138_1_p5, n3_to_8_decoder_74138_1_p6,
       n3_to_8_decoder_74138_1_p7, n3_to_8_decoder_74138_1_p8, n3_to_8_decoder_74138_1_p9,
       n3_to_8_decoder_74138_2_p10, n3_to_8_decoder_74138_2_p11, n3_to_8_decoder_74138_2_p12,
       n3_to_8_decoder_74138_2_p13, n3_to_8_decoder_74138_2_p14, n3_to_8_decoder_74138_2_p15,
       n3_to_8_decoder_74138_2_p16, n3_to_8_decoder_74138_2_p17, n3_to_8_decoder_74138_2_p18,
       n3_to_8_decoder_74138_2_p19, n4_to_1_mux_x2_74153_1_p10, n4_to_1_mux_x2_74153_1_p11,
       n4_to_1_mux_x2_74153_2_p12, n4_to_1_mux_x2_74153_2_p13, n4_to_1_mux_x2_74153_3_p12,
       n4_to_1_mux_x2_74153_3_p13, n4_to_1_mux_x2_74153_4_p12, n4_to_1_mux_x2_74153_4_p13,
       n4_to_1_mux_x2_74153_5_p12, n4_to_1_mux_x2_74153_5_p13, n4_to_1_mux_x2_74153_6_p12,
       n4_to_1_mux_x2_74153_6_p13, n4_to_1_mux_x2_74153_7_p11, n4_to_1_mux_x2_74153_7_p12,
       n4_to_1_mux_x2_74153_8_p16, n4_to_1_mux_x2_74153_8_p17, not_1_out, not_2_out, not_3_out, not_4_out,
       not_5_out, not_6_out, not_7_out, not_8_out, not_9_out, not_10_out, not_11_out, not_12_out, not_13_out,
       not_14_out, not_15_out, not_16_out, not_17_out, not_18_out, not_19_out, or_1_out, or_2_out, or_3_out,
       or_4_out, or_5_out, or_6_out, or_7_out, or_8_out, or_9_out, or_10_out, or_11_out, or_13_out,
       or_14_out, or_15_out, or_16_out, or_17_out, or_18_out, or_19_out, or_20_out, or_21_out, or_22_out,
       or_23_out, or_24_out, or_25_out, or_26_out, or_27_out, or_28_out, or_29_out, or_30_out, or_31_out,
       or_32_out, or_33_out, or_34_out, or_35_out, or_36_out, or_37_out, or_38_out, or_39_out, or_40_out,
       or_41_out, or_42_out, or_43_out, or_44_out, or_45_out, or_46_out, or_47_out, or_48_out, or_49_out,
       or_50_out, or_51_out, or_52_out, or_53_out, or_54_out, or_55_out, or_56_out, or_57_out, or_58_out,
       or_59_out, or_60_out, or_61_out, or_62_out, or_63_out, or_64_out, or_65_out, or_66_out, or_67_out,
       or_68_out, or_69_out, or_70_out, or_71_out, or_72_out, or_73_out, or_74_out, or_75_out, or_76_out;

  not not_1 (not_1_out, A1);
  // _3_to_8_decoder__74138 #(.Facing("east")) 3_to_8_decoder_74138_1: pin names not known; wires that end beside it: B0, B1, A0, n3_to_8_decoder_74138_1_p4, n3_to_8_decoder_74138_1_p5, n3_to_8_decoder_74138_1_p6, n3_to_8_decoder_74138_1_p7, n3_to_8_decoder_74138_1_p8, n3_to_8_decoder_74138_1_p9
  // _3_to_8_decoder__74138 #(.Facing("east")) 3_to_8_decoder_74138_2: pin names not known; wires that end beside it: B0, B1, A0, not_1_out, A1, A1, not_1_out, A1, not_1_out, n3_to_8_decoder_74138_2_p10, n3_to_8_decoder_74138_2_p11, n3_to_8_decoder_74138_2_p12, n3_to_8_decoder_74138_2_p13, n3_to_8_decoder_74138_2_p14, n3_to_8_decoder_74138_2_p15, n3_to_8_decoder_74138_2_p16, n3_to_8_decoder_74138_2_p17, n3_to_8_decoder_74138_2_p18, n3_to_8_decoder_74138_2_p19
  not not_2 (not_2_out, n3_to_8_decoder_74138_1_p4);
  not not_3 (not_3_out, n3_to_8_decoder_74138_1_p5);
  not not_4 (not_4_out, n3_to_8_decoder_74138_1_p6);
  not not_5 (not_5_out, n3_to_8_decoder_74138_1_p7);
  not not_6 (not_6_out, n3_to_8_decoder_74138_1_p8);
  not not_7 (not_7_out, n3_to_8_decoder_74138_1_p9);
  not not_8 (not_8_out, n3_to_8_decoder_74138_2_p10);
  not not_9 (not_9_out, n3_to_8_decoder_74138_2_p11);
  not not_10 (not_10_out, n3_to_8_decoder_74138_2_p12);
  not not_11 (not_11_out, n3_to_8_decoder_74138_2_p13);
  not not_12 (not_12_out, n3_to_8_decoder_74138_2_p14);
  not not_13 (not_13_out, n3_to_8_decoder_74138_2_p15);
  not not_14 (not_14_out, n3_to_8_decoder_74138_2_p16);
  not not_15 (not_15_out, n3_to_8_decoder_74138_2_p17);
  not not_16 (not_16_out, n3_to_8_decoder_74138_2_p18);
  not not_17 (not_17_out, n3_to_8_decoder_74138_2_p19);
  or or_1 (or_1_out, not_7_out, not_9_out);
  or or_2 (or_2_out, not_4_out, not_10_out);
  or or_3 (or_3_out, or_1_out, not_15_out);
  or or_4 (or_4_out, or_2_out, not_12_out);
  or or_5 (or_5_out, not_3_out, not_6_out);
  or or_6 (or_6_out, or_5_out, or_7_out);
  or or_7 (or_7_out, not_13_out, not_16_out);
  or or_8 (or_8_out, not_6_out, not_10_out);
  or or_9 (or_9_out, or_8_out, or_10_out);
  or or_10 (or_10_out, not_11_out, not_14_out);
  or or_11 (or_11_out, not_15_out, not_16_out);
  // OR_Gate or_12 has open pins: in0=or_9_out, in1=or_11_out, out=open
  or or_13 (or_13_out, not_13_out, not_16_out);
  or or_14 (or_14_out, not_9_out, not_12_out);
  or or_15 (or_15_out, not_8_out, not_11_out);
  or or_16 (or_16_out, not_5_out, not_8_out);
  or or_17 (or_17_out, not_11_out, not_14_out);
  or or_18 (or_18_out, not_5_out, not_14_out);
  or or_19 (or_19_out, not_4_out, not_7_out);
  or or_20 (or_20_out, not_4_out, not_9_out);
  or or_21 (or_21_out, not_10_out, not_15_out);
  or or_22 (or_22_out, not_4_out, not_7_out);
  or or_23 (or_23_out, not_12_out, not_13_out);
  or or_24 (or_24_out, not_3_out, not_6_out);
  or or_25 (or_25_out, not_6_out, not_10_out);
  or or_26 (or_26_out, or_25_out, or_27_out);
  or or_27 (or_27_out, not_14_out, not_11_out);
  or or_28 (or_28_out, not_15_out, not_16_out);
  or or_29 (or_29_out, or_14_out, not_15_out);
  or or_30 (or_30_out, or_16_out, or_17_out);
  or or_31 (or_31_out, or_19_out, not_10_out);
  or or_32 (or_32_out, or_20_out, or_21_out);
  or or_33 (or_33_out, or_23_out, not_16_out);
  or or_34 (or_34_out, or_24_out, not_7_out);
  or or_35 (or_35_out, or_26_out, or_28_out);
  or or_36 (or_36_out, not_2_out, not_3_out);
  or or_37 (or_37_out, or_36_out, or_38_out);
  or or_38 (or_38_out, not_4_out, not_5_out);
  or or_39 (or_39_out, not_7_out, not_8_out);
  or or_40 (or_40_out, or_39_out, or_41_out);
  or or_41 (or_41_out, not_9_out, not_12_out);
  or or_42 (or_42_out, not_13_out, not_17_out);
  or or_43 (or_43_out, or_37_out, or_40_out);
  or or_44 (or_44_out, or_43_out, or_42_out);
  not not_18 (not_18_out, O2);
  or or_45 (or_45_out, not_2_out, not_3_out);
  or or_46 (or_46_out, or_45_out, or_47_out);
  or or_47 (or_47_out, not_4_out, not_5_out);
  or or_48 (or_48_out, not_6_out, not_8_out);
  or or_49 (or_49_out, or_48_out, or_50_out);
  or or_50 (or_50_out, not_10_out, not_11_out);
  or or_51 (or_51_out, or_46_out, or_49_out);
  or or_52 (or_52_out, or_51_out, not_14_out);
  or or_53 (or_53_out, not_3_out, not_6_out);
  or or_54 (or_54_out, not_11_out, not_8_out);
  or or_55 (or_55_out, not_13_out, not_16_out);
  not not_19 (not_19_out, 1'b1);
  or or_56 (or_56_out, not_5_out, not_8_out);
  or or_57 (or_57_out, or_56_out, or_58_out);
  or or_58 (or_58_out, not_9_out, not_11_out);
  or or_59 (or_59_out, not_13_out, not_14_out);
  or or_60 (or_60_out, or_59_out, or_61_out);
  or or_61 (or_61_out, not_16_out, not_17_out);
  or or_62 (or_62_out, or_54_out, or_55_out);
  or or_63 (or_63_out, or_53_out, or_62_out);
  or or_64 (or_64_out, or_57_out, or_60_out);
  or or_65 (or_65_out, or_64_out, not_15_out);
  or or_66 (or_66_out, not_6_out, not_10_out);
  or or_67 (or_67_out, or_66_out, or_68_out);
  or or_68 (or_68_out, not_11_out, not_14_out);
  or or_69 (or_69_out, not_15_out, not_16_out);
  or or_70 (or_70_out, or_67_out, or_69_out);
  or or_71 (or_71_out, not_2_out, not_7_out);
  or or_72 (or_72_out, or_71_out, or_73_out);
  or or_73 (or_73_out, not_12_out, not_17_out);
  or or_74 (or_74_out, not_2_out, not_6_out);
  or or_75 (or_75_out, or_74_out, or_76_out);
  or or_76 (or_76_out, not_10_out, not_14_out);
  // _4_to_1_MUX__x2___74153 #(.Facing("east")) 4_to_1_mux_x2_74153_1: pin names not known; wires that end beside it: not_19_out, or_35_out, not_19_out, not_19_out, not_19_out, not_19_out, not_19_out, O2, not_18_out, n4_to_1_mux_x2_74153_1_p10, n4_to_1_mux_x2_74153_1_p11
  // _4_to_1_MUX__x2___74153 #(.Facing("east")) 4_to_1_mux_x2_74153_2: pin names not known; wires that end beside it: not_17_out, not_19_out, not_9_out, not_19_out, not_19_out, not_19_out, not_19_out, O0, O2, O1, not_18_out, n4_to_1_mux_x2_74153_2_p12, n4_to_1_mux_x2_74153_2_p13
  // _4_to_1_MUX__x2___74153 #(.Facing("east")) 4_to_1_mux_x2_74153_3: pin names not known; wires that end beside it: or_13_out, not_19_out, not_19_out, not_19_out, not_19_out, not_19_out, not_19_out, O0, O2, O1, not_18_out, n4_to_1_mux_x2_74153_3_p12, n4_to_1_mux_x2_74153_3_p13
  // _4_to_1_MUX__x2___74153 #(.Facing("east")) 4_to_1_mux_x2_74153_4: pin names not known; wires that end beside it: or_29_out, not_19_out, or_15_out, not_19_out, not_19_out, not_19_out, not_19_out, O0, O2, O1, not_18_out, n4_to_1_mux_x2_74153_4_p12, n4_to_1_mux_x2_74153_4_p13
  // _4_to_1_MUX__x2___74153 #(.Facing("east")) 4_to_1_mux_x2_74153_5: pin names not known; wires that end beside it: or_30_out, or_18_out, not_5_out, not_19_out, or_30_out, not_17_out, not_2_out, O0, O2, O1, not_18_out, n4_to_1_mux_x2_74153_5_p12, n4_to_1_mux_x2_74153_5_p13
  // _4_to_1_MUX__x2___74153 #(.Facing("east")) 4_to_1_mux_x2_74153_6: pin names not known; wires that end beside it: or_31_out, or_32_out, or_22_out, not_19_out, or_32_out, or_33_out, or_34_out, O0, O2, O1, not_18_out, n4_to_1_mux_x2_74153_6_p12, n4_to_1_mux_x2_74153_6_p13
  // _4_to_1_MUX__x2___74153 #(.Facing("east")) 4_to_1_mux_x2_74153_7: pin names not known; wires that end beside it: or_53_out, or_63_out, not_3_out, or_44_out, or_6_out, or_3_out, O0, O2, O1, not_18_out, n4_to_1_mux_x2_74153_7_p11, n4_to_1_mux_x2_74153_7_p12
  // _4_to_1_MUX__x2___74153 #(.Facing("east")) 4_to_1_mux_x2_74153_8: pin names not known; wires that end beside it: or_75_out, or_4_out, not_2_out, or_72_out, or_75_out, or_70_out, or_72_out, or_52_out, or_65_out, O0, O2, O0, O1, not_18_out, O1, n4_to_1_mux_x2_74153_8_p16, n4_to_1_mux_x2_74153_8_p17, L0
  or or_77 (S, n4_to_1_mux_x2_74153_1_p10, n4_to_1_mux_x2_74153_1_p11);
  or or_78 (L6, n4_to_1_mux_x2_74153_2_p12, n4_to_1_mux_x2_74153_2_p13);
  or or_79 (L5, n4_to_1_mux_x2_74153_3_p12, n4_to_1_mux_x2_74153_3_p13);
  or or_80 (L4, n4_to_1_mux_x2_74153_4_p12, n4_to_1_mux_x2_74153_4_p13);
  or or_81 (L3, n4_to_1_mux_x2_74153_5_p12, n4_to_1_mux_x2_74153_5_p13);
  or or_82 (L2, n4_to_1_mux_x2_74153_6_p12, n4_to_1_mux_x2_74153_6_p13);
  or or_83 (L1, n4_to_1_mux_x2_74153_7_p11, n4_to_1_mux_x2_74153_7_p12);
  or or_84 (L0, n4_to_1_mux_x2_74153_8_p16, n4_to_1_mux_x2_74153_8_p17);
endmodule
